// Logisim project 16-bit MIPS processor.circ as structural Verilog: 9 circuits, main circuit main
module main (
  input  [4:0] in_1,
  output [5:0] out_2,
  output [15:0] out_3,
  output [15:0] out_4,
  output [15:0] out_5
);

  wire alu_1_out_5, and_1_out, clock_1_out, controlunit_1_alusrc, controlunit_1_branch, controlunit_1_jump,
       controlunit_1_memread, controlunit_1_memtoreg, controlunit_1_memwrite, controlunit_1_regdst,
       controlunit_1_regwrite;
  wire [1:0] controlunit_1_aluop;
  wire [3:0] alucontrol_1_operation;
  wire [4:0] decoder_1_rd_11_15, decoder_1_rs_21_25, decoder_1_rt_16_20, decoder_1_shamt_6_10,
       multiplexer_1_out;
  wire [5:0] decoder_1_funct_0_5;
  wire [15:0] adder_1_out, adder_2_out, alu_1_alu_output, datamemory_1_readdata, decoder_1_address_0_15,
       decoder_1_jump_15_0, multiplexer_2_out, multiplexer_3_out, programcounter_1_output,
       register_1_readdata1, register_1_readdata2;
  wire [31:0] instructionmemory_1_instruction;

  programCounter programcounter_1 (.clock(clock_1_out), .\input (out_3), .\output (programcounter_1_output));
  Clock clock_1 (.out(clock_1_out));
  Adder #(.width(16)) adder_1 (.a(16'h1), .b(programcounter_1_output), .out(adder_1_out));  // open: cin, cout
  InstructionMemory instructionmemory_1 (
    .instruction(instructionmemory_1_instruction), .address(programcounter_1_output));
  Decoder decoder_1 (
    .Instruction_code(instructionmemory_1_instruction), .address_0_15(decoder_1_address_0_15),
    .funct_0_5(decoder_1_funct_0_5), .shamt_6_10(decoder_1_shamt_6_10), .rd_11_15(decoder_1_rd_11_15),
    .rt_16_20(decoder_1_rt_16_20), .rs_21_25(decoder_1_rs_21_25), .AluOp_26_31(out_2),
    .Jump_15_0(decoder_1_jump_15_0));
  controlUnit controlunit_1 (
    .RegDst(controlunit_1_regdst), .ALUSrc(controlunit_1_alusrc), .MemToReg(controlunit_1_memtoreg),
    .RegWrite(controlunit_1_regwrite), .MemRead(controlunit_1_memread), .MemWrite(controlunit_1_memwrite),
    .Branch(controlunit_1_branch), .in_1(out_2), .Jump(controlunit_1_jump), .aluOp(controlunit_1_aluop));
  Multiplexer #(.width(5)) multiplexer_1 (
    .in0(decoder_1_rt_16_20), .in1(decoder_1_rd_11_15), .out(multiplexer_1_out), .sel(controlunit_1_regdst));  // open: en
  Register register_1 (
    .writeData(out_4), .ReadData1(register_1_readdata1), .readData2(register_1_readdata2),
    .in_6(clock_1_out), .addressBit(multiplexer_1_out), .readRegister2(decoder_1_rt_16_20),
    .readRegister1(decoder_1_rs_21_25), .Regwrite(controlunit_1_regwrite));
  Multiplexer #(.width(16)) multiplexer_2 (
    .in0(register_1_readdata2), .in1(decoder_1_address_0_15), .out(multiplexer_2_out),
    .sel(controlunit_1_alusrc));  // open: en
  AluControl alucontrol_1 (.in_1(decoder_1_funct_0_5), .operation(alucontrol_1_operation), .Aluop(controlunit_1_aluop));
  Adder #(.width(16)) adder_2 (.a(adder_1_out), .b(decoder_1_address_0_15), .out(adder_2_out));  // open: cin, cout
  and and_1 (and_1_out, controlunit_1_branch, alu_1_out_5);
  ALU alu_1 (
    .Rs_Data(register_1_readdata1), .rt_data(multiplexer_2_out), .AluOp(alucontrol_1_operation),
    .shamt(decoder_1_shamt_6_10), .ALU_output(alu_1_alu_output), .out_5(alu_1_out_5));
  Multiplexer #(.width(16)) multiplexer_3 (
    .in0(adder_1_out), .in1(adder_2_out), .out(multiplexer_3_out), .sel(and_1_out));  // open: en
  dataMemory datamemory_1 (
    .WriteData_2(controlunit_1_memwrite), .readData(datamemory_1_readdata),
    .readMemory(controlunit_1_memread), .Address(alu_1_alu_output), .WriteData(register_1_readdata2),
    .clock(clock_1_out));
  Multiplexer #(.width(16)) multiplexer_4 (
    .in0(multiplexer_3_out), .in1(decoder_1_jump_15_0), .out(out_3), .sel(controlunit_1_jump));  // open: en
  Multiplexer #(.width(16)) multiplexer_5 (
    .in0(alu_1_alu_output), .in1(datamemory_1_readdata), .out(out_4), .sel(controlunit_1_memtoreg));  // open: en

  // Notes on the sheet:
  //   ADD
  //   Opcod(31-26)
  //   Address(15-0)
  //   rs(21-25)
  //   rd(11-15)
  //   memReg
  //   regWrite
  //   rt(16-20)
  //   RegDst
  //   Alusrc
  //   AluOp
  //   Add
  //   Alu result
  //   Branch
  //   Jump
  //   memRead
  //   memWrite
endmodule

module Register (
  input  [15:0] writeData,
  input  Regwrite,
  input  [4:0] readRegister1,
  input  [4:0] addressBit,
  input  [4:0] readRegister2,
  input  in_6,
  output [15:0] ReadData1,
  output [15:0] readData2
);

  wire and_1_out, and_2_out, and_3_out, and_4_out, and_5_out, and_6_out, and_7_out, and_8_out, and_9_out,
       and_10_out, and_11_out, and_12_out, and_13_out, and_14_out, and_15_out, and_16_out, decoder_1_out0,
       decoder_1_out1, decoder_1_out2, decoder_1_out3, decoder_1_out4, decoder_1_out5, decoder_1_out6,
       decoder_1_out7, decoder_1_out8, decoder_1_out9, decoder_1_out10, decoder_1_out11, decoder_1_out12,
       decoder_1_out13, decoder_1_out14, decoder_1_out15;
  wire [15:0] register_1_q, register_2_q, register_3_q, register_4_q, register_5_q, register_6_q,
       register_7_q, register_8_q, register_9_q, register_10_q, register_11_q, register_12_q, register_13_q,
       register_14_q, register_15_q, register_16_q;

  Decoder_part #(.select(4)) decoder_1 (
    .out0(decoder_1_out0), .out1(decoder_1_out1), .out2(decoder_1_out2), .out3(decoder_1_out3),
    .out4(decoder_1_out4), .out5(decoder_1_out5), .out6(decoder_1_out6), .out7(decoder_1_out7),
    .out8(decoder_1_out8), .out9(decoder_1_out9), .out10(decoder_1_out10), .out11(decoder_1_out11),
    .out12(decoder_1_out12), .out13(decoder_1_out13), .out14(decoder_1_out14), .out15(decoder_1_out15),
    .sel(addressBit[3:0]));  // open: en
  and and_1 (and_1_out, Regwrite, decoder_1_out0);
  and and_2 (and_2_out, Regwrite, decoder_1_out1);
  and and_3 (and_3_out, Regwrite, decoder_1_out2);
  and and_4 (and_4_out, Regwrite, decoder_1_out3);
  and and_5 (and_5_out, Regwrite, decoder_1_out4);
  and and_6 (and_6_out, Regwrite, decoder_1_out5);
  and and_7 (and_7_out, Regwrite, decoder_1_out6);
  and and_8 (and_8_out, Regwrite, decoder_1_out7);
  and and_9 (and_9_out, Regwrite, decoder_1_out8);
  and and_10 (and_10_out, Regwrite, decoder_1_out9);
  and and_11 (and_11_out, Regwrite, decoder_1_out10);
  and and_12 (and_12_out, Regwrite, decoder_1_out11);
  and and_13 (and_13_out, Regwrite, decoder_1_out12);
  and and_14 (and_14_out, Regwrite, decoder_1_out13);
  and and_15 (and_15_out, Regwrite, decoder_1_out14);
  and and_16 (and_16_out, Regwrite, decoder_1_out15);
  Register_part #(.width(16)) register_1 (.D(writeData), .en(and_1_out), .Q(register_1_q), .clk(in_6));  // open: clr
  Register_part #(.width(16)) register_2 (.D(writeData), .en(and_2_out), .Q(register_2_q), .clk(in_6));  // open: clr
  Register_part #(.width(16)) register_3 (.D(writeData), .en(and_3_out), .Q(register_3_q), .clk(in_6));  // open: clr
  Register_part #(.width(16)) register_4 (.D(writeData), .en(and_4_out), .Q(register_4_q), .clk(in_6));  // open: clr
  Register_part #(.width(16)) register_5 (.D(writeData), .en(and_5_out), .Q(register_5_q), .clk(in_6));  // open: clr
  Register_part #(.width(16)) register_6 (.D(writeData), .en(and_6_out), .Q(register_6_q), .clk(in_6));  // open: clr
  Register_part #(.width(16)) register_7 (.D(writeData), .en(and_7_out), .Q(register_7_q), .clk(in_6));  // open: clr
  Register_part #(.width(16)) register_8 (.D(writeData), .en(and_8_out), .Q(register_8_q), .clk(in_6));  // open: clr
  Register_part #(.width(16)) register_9 (.D(writeData), .en(and_9_out), .Q(register_9_q), .clk(in_6));  // open: clr
  Register_part #(.width(16)) register_10 (.D(writeData), .en(and_10_out), .Q(register_10_q), .clk(in_6));  // open: clr
  Register_part #(.width(16)) register_11 (.D(writeData), .en(and_11_out), .Q(register_11_q), .clk(in_6));  // open: clr
  Register_part #(.width(16)) register_12 (.D(writeData), .en(and_12_out), .Q(register_12_q), .clk(in_6));  // open: clr
  Register_part #(.width(16)) register_13 (.D(writeData), .en(and_13_out), .Q(register_13_q), .clk(in_6));  // open: clr
  Register_part #(.width(16)) register_14 (.D(writeData), .en(and_14_out), .Q(register_14_q), .clk(in_6));  // open: clr
  Register_part #(.width(16)) register_15 (.D(writeData), .en(and_15_out), .Q(register_15_q), .clk(in_6));  // open: clr
  Register_part #(.width(16)) register_16 (.D(writeData), .en(and_16_out), .Q(register_16_q), .clk(in_6));  // open: clr
  Multiplexer #(.select(4), .width(16)) multiplexer_1 (
    .in0(register_1_q), .in1(register_2_q), .in2(register_3_q), .in3(register_4_q), .in4(register_5_q),
    .in5(register_6_q), .in6(register_7_q), .in7(register_8_q), .in8(register_9_q), .in9(register_10_q),
    .in10(register_11_q), .in11(register_12_q), .in12(register_13_q), .in13(register_14_q),
    .in14(register_15_q), .in15(register_16_q), .out(ReadData1), .sel(readRegister1[3:0]));  // open: en
  Multiplexer #(.select(4), .width(16)) multiplexer_2 (
    .in0(register_1_q), .in1(register_2_q), .in2(register_3_q), .in3(register_4_q), .in4(register_5_q),
    .in5(register_6_q), .in6(register_7_q), .in7(register_8_q), .in8(register_9_q), .in9(register_10_q),
    .in10(register_11_q), .in11(register_12_q), .in12(register_13_q), .in13(register_14_q),
    .in14(register_15_q), .in15(register_16_q), .out(readData2), .sel(readRegister2[3:0]));  // open: en
endmodule

module ALU (
  input  [15:0] Rs_Data,
  input  [15:0] rt_data,
  input  [4:0] shamt,
  input  [3:0] AluOp,
  output out_5,
  output [15:0] ALU_output
);

  wire [15:0] adder_1_out, and_1_out, nor_1_out, or_1_out, shifter_1_out, shifter_2_out, subtractor_1_out,
       xor_1_out;

  Adder #(.width(16)) adder_1 (.a(Rs_Data), .b(rt_data), .out(adder_1_out));  // open: cin, cout
  Subtractor #(.width(16)) subtractor_1 (.a(Rs_Data), .b(rt_data), .out(subtractor_1_out));  // open: bin, bout
  assign or_1_out = Rs_Data | rt_data;  // OR_Gate or_1, 16 bits wide
  assign and_1_out = Rs_Data & rt_data;  // AND_Gate and_1, 16 bits wide
  assign xor_1_out = Rs_Data ^ rt_data;  // XOR_Gate xor_1, 16 bits wide
  assign nor_1_out = ~(Rs_Data | rt_data);  // NOR_Gate nor_1, 16 bits wide
  Shifter #(.width(16)) shifter_1 (.in(Rs_Data), .\dist (shamt[3:0]), .out(shifter_1_out));
  Shifter #(.width(16), .shift("lr")) shifter_2 (.in(Rs_Data), .\dist (shamt[3:0]), .out(shifter_2_out));
  Multiplexer #(.select(4), .width(16)) multiplexer_1 (
    .in0(adder_1_out), .in1(subtractor_1_out), .in2(or_1_out), .in3(and_1_out), .in4(xor_1_out),
    .in5(nor_1_out), .in6(shifter_1_out), .in7(shifter_2_out), .out(ALU_output), .sel(AluOp));  // open: in8, in9, in10, in11, in12, in13, in14, in15, en
  nor nor_2 (out_5, ALU_output[0], ALU_output[1], ALU_output[2], ALU_output[3], ALU_output[4], ALU_output[5], ALU_output[6], ALU_output[7], ALU_output[9], ALU_output[10], ALU_output[11], ALU_output[12], ALU_output[13], ALU_output[14], ALU_output[15], ALU_output[8]);
endmodule

// Control unit
module controlUnit (
  input  [5:0] in_1,
  output RegDst,
  output ALUSrc,
  output MemToReg,
  output RegWrite,
  output MemRead,
  output MemWrite,
  output Branch,
  output [1:0] aluOp,
  output Jump
);

  and and_1 (aluOp[1], ~in_1[5], ~in_1[4], ~in_1[3], ~in_1[2], ~in_1[1], ~in_1[0]);  // AND_Gate
  and and_2 (MemRead, in_1[5], ~in_1[4], ~in_1[3], ~in_1[2], in_1[1], in_1[0]);  // AND_Gate
  and and_3 (MemWrite, in_1[5], ~in_1[4], in_1[3], ~in_1[2], in_1[1], in_1[0]);  // AND_Gate
  and and_4 (aluOp[0], ~in_1[5], ~in_1[4], ~in_1[3], in_1[2], ~in_1[1], ~in_1[0]);  // AND_Gate
  or or_1 (ALUSrc, MemRead, MemWrite);
  or or_2 (RegWrite, aluOp[1], MemRead);
  and and_5 (Jump, ~in_1[5], ~in_1[4], ~in_1[3], ~in_1[2], ~in_1[1], in_1[0]);  // AND_Gate

  assign Branch = aluOp[0];
  assign MemToReg = MemRead;
  assign RegDst = aluOp[1];

  // Notes on the sheet:
  //   R-Type
  //   lw
  //   sw
  //   beq
  //   RegDst
  //   AluOp1
  //   Aluop0
  //   Jump
  //   AluSrc
  //   MemtoReg
  //   RegWrite
  //   MemRead
  //   MemWrite
  //   Branch
endmodule

// IM
module InstructionMemory (
  input  [15:0] address,
  output [31:0] instruction
);

  ROM #(.addrWidth(16), .dataWidth(32)) rom_1 (.addr(address), .data(instruction));  // open: sel

  // Notes on the sheet:
  //   contents of rom_1 (hex, n*v repeats v):
  //   8c010001 8c020002 221800 10220004 4*0 4000003
endmodule

// DM
module dataMemory (
  input  [15:0] Address,
  input  [15:0] WriteData,
  input  readMemory,
  input  WriteData_2,
  input  clock,
  output [15:0] readData
);

  RAM #(.addrWidth(16), .dataWidth(16), .bus("separate")) ram_1 (
    .addr(Address), .din(WriteData), .data(readData), .str(WriteData_2), .clk(clock), .ld(readMemory));  // open: sel, clr
endmodule

// PC
module programCounter (
  input  [15:0] \input ,
  input  clock,
  output [15:0] \output 
);

  Register_part #(.width(16)) register_1 (.D(\input ), .en(1'b1), .Q(\output ), .clk(clock));  // open: clr
endmodule

// Alu control
module AluControl (
  input  [5:0] in_1,
  input  [1:0] Aluop,
  output [3:0] operation
);

  wire and_1_out, and_2_out, and_3_out, and_4_out, not_1_out, not_2_out, not_3_out, not_4_out, not_5_out,
       not_6_out, or_1_out, or_2_out;

  not not_1 (not_1_out, Aluop[0]);
  not not_2 (not_2_out, Aluop[1]);
  not not_3 (not_3_out, in_1[3]);
  not not_4 (not_4_out, in_1[1]);
  not not_5 (not_5_out, in_1[2]);
  not not_6 (not_6_out, in_1[0]);
  and and_1 (and_1_out, not_3_out, in_1[2]);
  or or_1 (or_1_out, Aluop[1], Aluop[0]);
  and and_2 (and_2_out, not_3_out, in_1[1]);
  and and_3 (and_3_out, not_3_out, in_1[0], not_4_out);
  and and_4 (and_4_out, not_3_out, in_1[1], not_6_out);
  or or_2 (or_2_out, and_3_out, and_4_out);
  and and_5 (operation[2], and_1_out, or_1_out);
  and and_6 (operation[1], or_1_out, and_2_out);
  and and_7 (operation[0], or_1_out, or_2_out);

  assign operation[3] = 1'b0;
endmodule

module Decoder (
  input  [31:0] Instruction_code,
  output [15:0] Jump_15_0,
  output [15:0] address_0_15,
  output [5:0] funct_0_5,
  output [4:0] shamt_6_10,
  output [4:0] rd_11_15,
  output [4:0] rt_16_20,
  output [4:0] rs_21_25,
  output [5:0] AluOp_26_31
);


  assign address_0_15 = Instruction_code[15:0];
  assign AluOp_26_31 = Instruction_code[31:26];
  assign funct_0_5 = Instruction_code[5:0];
  assign Jump_15_0 = Instruction_code[15:0];
  assign rd_11_15 = Instruction_code[15:11];
  assign rs_21_25 = Instruction_code[25:21];
  assign rt_16_20 = Instruction_code[20:16];
  assign shamt_6_10 = Instruction_code[10:6];
endmodule
